# Fritzing sketch led-and-switch (saved by Fritzing 0.9.3b)
breadboards: 1

parts:
  Part1 = Arduino Uno (Rev3)
  LED1 = LED - 5mm [color="Red (633nm)" package="5 mm [THT]"]
  S1 = Pushbutton [package=THT]
  R1 = Resistor [tolerance=±5% resistance=220 package=THT]

nets:
  N1: Part1.D13/SCK, R1.Pin_1
  N2: Part1.GND, LED1.cathode
  N3: LED1.anode, S1.leg1
  N4: S1.leg0, R1.Pin_0
